# Fritzing sketch smart-movie-ticket (saved by Fritzing 0.9.3b)
breadboards: 1

parts:
  Part1 = Arduino Uno (Rev3) - ICSP
  Part2 = LCD1602-I2C
  PCB2 = RTC_DS1302_module
  Part3 = RFID-RC522-v2
  R1 = Resistor [tolerance=±5% resistance=220 package="2512 [SMD]"]
  LED1 = LED - 3mm [color="Red (633nm)" package="3 mm [THT]"]
  J1 = Piezo Speaker

nets:
  N1: Part1.A4/SDA, Part2.SDA
  N2: Part1.A5/SCL, Part2.SCL
  N3: Part1.D9_PWM, Part3.RST
  N4: Part1.D10_PWM/SS, Part3.SDA
  N5: Part1.D11_PWM/MOSI, Part3.MOSI
  N6: Part1.D12/MISO, Part3.MISO
  N7: Part1.D13/SCK, Part3.SCK
  GND: Part1.GND, Part2.GND, PCB2.GND, Part3.GND, LED1.anode, J1.pin1
  N8: Part1.D3_PWM, J1.pin2
  N9: Part1.D4, R1.Pin_0
  N10: Part1.D5_PWM, PCB2.RST
  N11: Part1.D6_PWM, PCB2.DAT
  N12: Part1.D7, PCB2.CLK
  VCC: Part1.5V, Part2.VCC, PCB2.VCC
  N13: R1.Pin_1, LED1.cathode

custom parts:
  LCD1602-I2C: A standard character display, usually with 2x16 characters. Comes in many colors with LCM1602 IIC attached.
  RTC_DS1302_module: Arduino module DS1302 SPI Real Time Clock
  RFID-RC522-v2: A simple China made RFID-RC522 Reader; do check the pin labels, as this is a MFRC522 based clone.
